# Fritzing sketch Schaltplan (saved by Fritzing 0.9.3b)

parts:
  Raspberry_Pi_1 = Raspberry Pi 3 [part_number=RPI-3-V1.2]
  U1 = LIPO-1000mAh [package=lipo-1000]
  S1 = H-Bridge with L298N
  Q1 = DC-DC Step Down LM2596S [package=breakout]
  M1 = DC Motor
  M2 = DC Motor
  M4 = DC Motor
  M3 = DC Motor
  hc-sr1 = hc-sr04
  hc-sr2 = hc-sr04
  R1 = Resistor [tolerance=±5% resistance=330 package=THT]
  R2 = Resistor [tolerance=±5% resistance=470 package=THT]
  R3 = Resistor [tolerance=±5% resistance=330 package=THT]
  R4 = Resistor [tolerance=±5% resistance=470 package=THT]

nets (from the breadboard view):
  N1: Raspberry_Pi_1.GIPO17, S1.IN3
  N2: Raspberry_Pi_1.GIPO27, S1.IN4
  N3: Raspberry_Pi_1.GIPO22, S1.ENB
  N4: Raspberry_Pi_1.GIPO10, S1.ENA
  N5: Raspberry_Pi_1.GIPO9, S1.IN1
  N6: Raspberry_Pi_1.GIPO11, S1.IN2
  GND: Raspberry_Pi_1.GND, Q1.OUT-, hc-sr1.GND, hc-sr2.GND
  N7: Raspberry_Pi_1.GIPO21, R3.Pin_0, R4.Pin_1
  N8: Raspberry_Pi_1.GIPO20, hc-sr2.Trig
  N9: Raspberry_Pi_1.GIPO16, R1.Pin_0, R2.Pin_1
  N10: Raspberry_Pi_1.GIPO12, hc-sr1.Trig
  N11: U1.+, S1.12V
  N12: U1.-, S1.GND
  N13: S1.M1-01, M1.pin_2, M2.pin_2
  N14: S1.M1-02, M1.pin_1, M2.pin_1
  N15: S1.M2-01, M4.pin_2, M3.pin_2
  N16: S1.M2-02, M4.pin_1, M3.pin_1
  N17: hc-sr1.Echo, R1.Pin_1
  N18: hc-sr2.Echo, R3.Pin_1

custom parts:
  H-Bridge with L298N: h-bridge
